// Logisim project Blake3000.circ as structural Verilog
module ALU (
  input  SEL,
  input  [7:0] A,
  input  [7:0] B,
  output [7:0] O
);

  wire [7:0] adder_1_out, subtractor_1_out;

  Adder adder_1 (.a(A), .b(B), .out(adder_1_out));  // open: cin, cout
  Multiplexer #(.width(8)) multiplexer_1 (.in0(adder_1_out), .in1(subtractor_1_out), .out(O), .sel(SEL));
  Subtractor subtractor_1 (.a(A), .b(B), .out(subtractor_1_out));  // open: bin, bout
endmodule
